# Fritzing sketch xuxesbot_conexiones_recomedada (saved by Fritzing 0.9.2b)
breadboards: 1

parts:
  Parte1 = Arduino Uno (Rev3)
  IC1 = L293D [package=THT]
  Parte3 = Bluetooth HC-06
  BAT1 = BC9VPC [package=bc9vpc]
  VCC1 = 4 x AAA Battery Mount
  LEFT_MOTOR = DC Motor
  RIGHT_MOTOR = DC Motor

nets:
  N1: Parte1.D10_PWM/SS, Parte3.RXD
  N2: Parte1.D11_PWM/MOSI, Parte3.TXD
  N3: Parte1.D2, IC1.In_1
  N4: Parte1.D3_PWM, IC1.Enable_1
  N5: Parte1.D4, IC1.In_2
  N6: Parte1.D5_PWM, IC1.In_3
  N7: Parte1.D6_PWM, IC1.Enable_2
  N8: Parte1.D7, IC1.In_4
  5V: Parte1.5V, IC1.+V, Parte3.VCC
  GND: Parte1.GND, IC1.0V, IC1.+Vmotor, Parte3.GND, BAT1.V-, VCC1.-, VCC1.+
  N9: Parte1.VIN, BAT1.V+
  N10: IC1.Out_1_(_Controlled_by_Enable_1_), RIGHT_MOTOR.pin_2
  N11: IC1.Out_2_(_Controlled_by_Enable_1_), RIGHT_MOTOR.pin_1
  N12: IC1.Out_3_(_Controlled_by_Enable_2_), LEFT_MOTOR.pin_1
  N13: IC1.Out_4_(_Controlled_by_Enable_2_), LEFT_MOTOR.pin_2
